// Logisim project ALU.circ as structural Verilog: 2 circuits, main circuit ALU
module ALU (
  input  [31:0] A,
  input  [31:0] B,
  input  [4:0] Shift,
  input  CarryIn,
  input  [3:0] Codop,
  output [31:0] S,
  output [3:0] Flags
);

  wire adder_1_cout, adder_2_cout, bitselector_3_out, bitselector_4_out, bitselector_5_out, carryLSL,
       carryLSR, not_1_out, overflowdetector_1_v, subtractor_2_bout, subtractor_3_bout;
  wire [4:0] negator_1_out, subtractor_1_out;
  wire [31:0] adder_1_out, adder_2_out, and_1_out, and_2_out, and_3_out, multiplier_1_out, negator_2_out,
       not_2_out, not_3_out, or_1_out, res, shifter_1_out, shifter_2_out, shifter_3_out, shifter_4_out,
       subtractor_2_out, subtractor_3_out, xor_1_out;

  not not_1 (not_1_out, CarryIn);
  Subtractor #(.width(5)) subtractor_1 (.a(Shift), .b(5'b00001), .out(subtractor_1_out));  // open: bin, bout
  Negator #(.width(5)) negator_1 (.in(Shift), .out(negator_1_out));
  assign not_2_out = ~A;  // NOT_Gate not_2, 32 bits wide
  assign not_3_out = ~A;  // NOT_Gate not_3, 32 bits wide
  BitSelector #(.width(32)) bitselector_1 (.in(B), .out(carryLSR), .sel(subtractor_1_out));
  BitSelector #(.width(32)) bitselector_2 (.in(B), .out(carryLSL), .sel(negator_1_out));
  assign and_1_out = A & B;  // AND_Gate and_1, 32 bits wide
  assign xor_1_out = A ^ B;  // XOR_Gate xor_1, 32 bits wide
  Shifter #(.width(32)) shifter_1 (.in(B), .\dist (Shift), .out(shifter_1_out));
  Shifter #(.shift("lr"), .width(32)) shifter_2 (.in(B), .\dist (Shift), .out(shifter_2_out));
  Shifter #(.shift("ar"), .width(32)) shifter_3 (.in(B), .\dist (Shift), .out(shifter_3_out));
  Adder #(.width(32)) adder_1 (.a(A), .b(B), .out(adder_1_out), .cin(CarryIn), .cout(adder_1_cout));
  Subtractor #(.width(32)) subtractor_2 (
    .a(B), .b(A), .out(subtractor_2_out), .bin(not_1_out), .bout(subtractor_2_bout));
  Shifter #(.shift("rr"), .width(32)) shifter_4 (.in(B), .\dist (Shift), .out(shifter_4_out));
  assign and_2_out = A & B;  // AND_Gate and_2, 32 bits wide
  Negator #(.width(32)) negator_2 (.in(A), .out(negator_2_out));
  Subtractor #(.width(32)) subtractor_3 (.a(B), .b(A), .out(subtractor_3_out), .bout(subtractor_3_bout));  // open: bin
  Adder #(.width(32)) adder_2 (.a(A), .b(B), .out(adder_2_out), .cout(adder_2_cout));  // open: cin
  assign or_1_out = A | B;  // OR_Gate or_1, 32 bits wide
  Multiplier #(.mode("twosComplement"), .width(32)) multiplier_1 (
    .a(A), .b(B), .out(multiplier_1_out));  // open: cin, cout
  assign and_3_out = not_2_out & B;  // AND_Gate and_3, 32 bits wide
  Multiplexer #(.select(4), .width(32)) multiplexer_1 (
    .in0(and_1_out), .in1(xor_1_out), .in2(shifter_1_out), .in3(shifter_2_out), .in4(shifter_3_out),
    .in5(adder_1_out), .in6(subtractor_2_out), .in7(shifter_4_out), .in8(and_2_out), .in9(negator_2_out),
    .in10(subtractor_3_out), .in11(adder_2_out), .in12(or_1_out), .in13(multiplier_1_out), .in14(and_3_out),
    .in15(not_3_out), .out(res), .sel(Codop));
  BitSelector #(.width(32)) bitselector_3 (.in(A), .out(bitselector_3_out), .sel({5{1'b1}}));
  BitSelector #(.width(32)) bitselector_4 (.in(B), .out(bitselector_4_out), .sel({5{1'b1}}));
  BitSelector #(.width(32)) bitselector_5 (.in(res), .out(bitselector_5_out), .sel({5{1'b1}}));
  Comparator #(.width(32)) comparator_1 (.a(res), .b({32{1'b0}}), .eq(Flags[2]), .lt(Flags[3]));  // open: gt
  Multiplexer #(.select(4)) multiplexer_2 (
    .in0(1'b0), .in1(1'b0), .in2(carryLSL), .in3(carryLSR), .in4(carryLSR), .in5(adder_1_cout),
    .in6(subtractor_2_bout), .in7(carryLSR), .in8(1'b0), .in9(1'b0), .in10(subtractor_3_bout),
    .in11(adder_2_cout), .in12(1'b0), .in13(1'b0), .in14(1'b0), .in15(1'b0), .out(Flags[1]), .sel(Codop));
  OverflowDetector overflowdetector_1 (
    .a(bitselector_3_out), .b(bitselector_4_out), .r(bitselector_5_out), .v(overflowdetector_1_v));
  Multiplexer #(.select(4), .width(32)) multiplexer_3 (
    .in0(res), .in1(res), .in2(res), .in3(res), .in4(res), .in5(res), .in6(res), .in7(res), .in8(B),
    .in9(res), .in10(B), .in11(B), .in12(res), .in13(res), .in14(res), .in15(res), .out(S), .sel(Codop));
  Multiplexer #(.select(4)) multiplexer_4 (
    .in0(1'b0), .in1(1'b0), .in2(1'b0), .in3(1'b0), .in4(1'b0), .in5(overflowdetector_1_v),
    .in6(overflowdetector_1_v), .in7(1'b0), .in8(1'b0), .in9(1'b0), .in10(1'b0), .in11(overflowdetector_1_v),
    .in12(overflowdetector_1_v), .in13(1'b0), .in14(1'b0), .in15(1'b0), .out(Flags[0]), .sel(Codop));

  // Other names for the same wires on the sheet: v = Flags[0]
endmodule

module OverflowDetector (
  input  a,
  input  b,
  input  r,
  output v
);

  wire and_1_out, and_2_out, not_1_out, not_2_out, not_3_out;

  not not_1 (not_1_out, a);
  not not_2 (not_2_out, b);
  not not_3 (not_3_out, r);
  and and_1 (and_1_out, not_1_out, not_2_out, r);
  or or_1 (v, and_1_out, and_2_out);
  and and_2 (and_2_out, a, b, not_3_out);
endmodule
