// Logisim project Ctl_Conditional.circ as structural Verilog: 1 circuit, main circuit Conditional
module Conditional (
  input  Enable,
  input  [15:0] Instruction,
  input  Z,
  input  C,
  input  N,
  input  V,
  output [10:0] Offset,
  output Verified
);

  wire and_1_out, and_2_out, comparator_1_eq, multiplexer_1_out, multiplexer_3_out, not_1_out, not_2_out,
       not_3_out, not_4_out, not_5_out, or_1_out, or_2_out, xor_1_out, xor_2_out;
  wire [3:0] bitselector_1_out;
  wire [10:0] bit_extender_1_out, bit_extender_2_out, multiplexer_2_out;

  not not_1 (not_1_out, Z);
  not not_2 (not_2_out, C);
  not not_3 (not_3_out, N);
  not not_4 (not_4_out, V);
  Comparator #(.mode("unsigned"), .width(4)) comparator_1 (
    .a(4'b1110), .b(Instruction[15:12]), .eq(comparator_1_eq));  // open: gt, lt
  xor xor_1 (xor_1_out, N, V);
  and and_1 (and_1_out, C, not_1_out);
  or or_1 (or_1_out, not_2_out, Z);
  xor xor_2 (xor_2_out, N, V);
  and and_2 (and_2_out, not_1_out, ~xor_1_out);  // AND_Gate
  or or_2 (or_2_out, xor_1_out, Z);
  assign bit_extender_1_out = {{10{Enable}}, Enable};  // Bit_Extender bit_extender_1
  not not_5 (not_5_out, xor_2_out);
  BitSelector #(.group(4), .width(16)) bitselector_1 (.in(Instruction), .out(bitselector_1_out), .sel(2'b10));
  Multiplexer #(.select(4)) multiplexer_1 (
    .in0(Z), .in1(not_1_out), .in2(C), .in3(not_2_out), .in4(N), .in5(not_3_out), .in6(V), .in7(not_4_out),
    .in8(and_1_out), .in9(or_1_out), .in10(not_5_out), .in11(xor_2_out), .in12(and_2_out), .in13(or_2_out),
    .in14(1'b1), .in15(1'b0), .out(multiplexer_1_out), .sel(bitselector_1_out));
  Multiplexer #(.width(11)) multiplexer_2 (
    .in0(bit_extender_2_out), .in1(Instruction[10:0]), .out(multiplexer_2_out), .sel(comparator_1_eq));
  Multiplexer multiplexer_3 (.in0(multiplexer_1_out), .in1(1'b1), .out(multiplexer_3_out), .sel(comparator_1_eq));
  assign Offset = bit_extender_1_out & multiplexer_2_out;  // AND_Gate and_3, 11 bits wide
  and and_4 (Verified, Enable, multiplexer_3_out);
  assign bit_extender_2_out = {{10{Verified}}, Verified};  // Bit_Extender bit_extender_2
endmodule
