// Logisim project Ctl_Data_Processing.circ as structural Verilog: 1 circuit, main circuit Data_Processing
module Data_Processing (
  input  Enable,
  input  [15:0] Instruction,
  output [2:0] Rd,
  output [2:0] Rn,
  output [2:0] Rm,
  output [3:0] ALU_Opcode,
  output [3:0] Flags_Update_Mask
);

  wire [1:0] multiplexer_2_out;
  wire [2:0] enable3, multiplexer_3_out, multiplexer_4_out, multiplexer_5_out;
  wire [3:0] bit_extender_1_out;

  Multiplexer #(.select(4)) multiplexer_1 (
    .in0(1'b1), .in1(1'b1), .in2(1'b1), .in3(1'b1), .in4(1'b1), .in5(1'b1), .in6(1'b1), .in7(1'b1),
    .in8(1'b1), .in9(1'b1), .in10(1'b1), .in11(1'b1), .in12(1'b1), .in13(1'b0), .in14(1'b1), .in15(1'b1),
    .out(multiplexer_2_out[1]), .sel(Instruction[9:6]));
  assign bit_extender_1_out = {{3{Enable}}, Enable};  // Bit_Extender bit_extender_1
  assign enable3 = {{2{Enable}}, Enable};  // Bit_Extender bit_extender_2
  Multiplexer #(.select(4)) multiplexer_2 (
    .in0(1'b0), .in1(1'b0), .in2(1'b0), .in3(1'b0), .in4(1'b0), .in5(1'b1), .in6(1'b1), .in7(1'b0),
    .in8(1'b0), .in9(1'b1), .in10(1'b1), .in11(1'b1), .in12(1'b0), .in13(1'b0), .in14(1'b0), .in15(1'b0),
    .out(multiplexer_2_out[0]), .sel(Instruction[9:6]));
  assign Rm = enable3 & multiplexer_3_out;  // AND_Gate and_1, 3 bits wide
  Multiplexer #(.select(4), .width(3)) multiplexer_3 (
    .in0(Instruction[5:3]), .in1(Instruction[5:3]), .in2(Instruction[5:3]), .in3(Instruction[5:3]),
    .in4(Instruction[5:3]), .in5(Instruction[5:3]), .in6(Instruction[5:3]), .in7(Instruction[5:3]),
    .in8(Instruction[5:3]), .in9(3'b000), .in10(Instruction[5:3]), .in11(Instruction[5:3]),
    .in12(Instruction[5:3]), .in13(Instruction[2:0]), .in14(Instruction[5:3]), .in15(Instruction[5:3]),
    .out(multiplexer_3_out), .sel(Instruction[9:6]));
  Multiplexer #(.select(4), .width(3)) multiplexer_4 (
    .in0(Instruction[2:0]), .in1(Instruction[2:0]), .in2(Instruction[2:0]), .in3(Instruction[2:0]),
    .in4(Instruction[2:0]), .in5(Instruction[2:0]), .in6(Instruction[2:0]), .in7(Instruction[2:0]),
    .in8(Instruction[2:0]), .in9(Instruction[5:3]), .in10(Instruction[2:0]), .in11(Instruction[2:0]),
    .in12(Instruction[2:0]), .in13(Instruction[5:3]), .in14(Instruction[2:0]), .in15(3'b000),
    .out(multiplexer_4_out), .sel(Instruction[9:6]));
  assign ALU_Opcode = Instruction[9:6] & bit_extender_1_out;  // AND_Gate and_2, 4 bits wide
  assign Rn = enable3 & multiplexer_4_out;  // AND_Gate and_3, 3 bits wide
  assign Flags_Update_Mask = bit_extender_1_out & {2'b11, multiplexer_2_out};  // AND_Gate and_4, 4 bits wide
  Multiplexer #(.select(4), .width(3)) multiplexer_5 (
    .in0(Instruction[2:0]), .in1(Instruction[2:0]), .in2(Instruction[2:0]), .in3(Instruction[2:0]),
    .in4(Instruction[2:0]), .in5(Instruction[2:0]), .in6(Instruction[2:0]), .in7(Instruction[2:0]),
    .in8(Instruction[2:0]), .in9(Instruction[2:0]), .in10(Instruction[2:0]), .in11(Instruction[2:0]),
    .in12(Instruction[2:0]), .in13(Instruction[2:0]), .in14(Instruction[2:0]), .in15(Instruction[2:0]),
    .out(multiplexer_5_out), .sel(Instruction[9:6]));
  assign Rd = multiplexer_5_out & enable3;  // AND_Gate and_5, 3 bits wide

  // Notes on the sheet:
  //   Pull output low on Enable = 0
endmodule
