// Logisim project Ctl_Load_Store.circ as structural Verilog: 1 circuit, main circuit Load_Store
module Load_Store (
  input  Enable,
  input  [15:0] Instruction,
  input  Clk,
  input  [31:0] Stack_Pointer,
  input  Reset,
  output Load,
  output Store,
  output PC_Hold,
  output [2:0] Rmd,
  output [31:0] RAM_Addr
);

  wire and_4_out, d_ff_1_q, d_ff_1_qn, not_1_out, not_2_out, or_1_out;
  wire [2:0] bit_extender_1_out;
  wire [31:0] addr, bit_extender_2_out, bit_extender_3_out;

  not not_1 (not_1_out, Instruction[11]);
  assign bit_extender_1_out = {{2{Enable}}, Enable};  // Bit_Extender bit_extender_1
  assign bit_extender_2_out = {{31{Enable}}, Enable};  // Bit_Extender bit_extender_2
  and and_1 (Store, Enable, not_1_out);
  assign Rmd = Instruction[10:8] & bit_extender_1_out;  // AND_Gate and_2, 3 bits wide
  assign RAM_Addr = addr & bit_extender_2_out;  // AND_Gate and_3, 32 bits wide
  assign bit_extender_3_out = {{24{Instruction[7]}}, Instruction[7:0]};  // Bit_Extender bit_extender_3
  Adder #(.width(32)) adder_1 (.a(bit_extender_3_out), .b(Stack_Pointer), .out(addr));  // open: cin, cout
  not not_2 (not_2_out, d_ff_1_q);
  D_Flip_Flop #(.trigger("falling")) d_ff_1 (
    .D(and_4_out), .clk(Clk), .Q(d_ff_1_q), .Qn(d_ff_1_qn), .reset(or_1_out));  // open: preset
  and and_4 (and_4_out, not_2_out, Instruction[11]);
  or or_1 (or_1_out, ~Enable, Reset, ~Instruction[11]);  // OR_Gate
  and and_5 (Load, Enable, Instruction[11], d_ff_1_q);
  // Probe on d_ff_1_q
  and and_6 (PC_Hold, d_ff_1_qn, Enable, Instruction[11]);

  // Other names for the same wires on the sheet: imm8[7:0] = Instruction[7:0]; RegDest[2:0] = Instruction[10:8];
  //   cond = Instruction[11]

  // Notes on the sheet:
  //   Instruction: pull=down
  //   On s'assure d'activer store
  //   L'addition du Stack_Pointer et de Imm8 pour calculer une adresse mémoire cible
  //   Imm8 (Immediate 8 bits) : Les 8 bits représentant une valeur
  //   ²
  //   RegDest (Register destination) : Les bits spécifiant le registre de destination.
  //   cond (Condition) : Bits représentant une condition ou un code d'opération spécifique.
endmodule
