// Logisim project Ctl_Shift_Add_Sub_Mov.circ as structural Verilog: 1 circuit, main circuit Shift_Add_Sub_Mov
module Shift_Add_Sub_Mov (
  input  Enable,
  input  [15:0] Instruction,
  output [3:0] Flags_Update_Mask,
  output Carry,
  output Imm32_Enable,
  output [2:0] Rm,
  output [2:0] Rn,
  output [2:0] Rd,
  output [4:0] Imm5,
  output [31:0] Imm32,
  output [3:0] ALU_Opcode
);

  wire and_1_out, and_2_out, and_3_out, and_4_out, and_5_out, and_6_out, and_7_out, and_9_out, and_10_out,
       and_11_out, Carry_t, IsMOV, or_5_out, Rdn, UseImm5, UseImm32, UseRm, UseRn;
  wire [1:0] FlagsMask;
  wire [2:0] and_15_out, bit_extender_3_out, bit_extender_6_out, bit_extender_7_out, bit_extender_8_out,
       bit_extender_11_out, multiplexer_4_out, RdMux;
  wire [3:0] bit_extender_5_out, bit_extender_10_out, multiplexer_5_out, priority_encoder_1_out;
  wire [4:0] and_17_out, bit_extender_4_out, bit_extender_12_out;
  wire [7:0] bit_extender_1_out, multiplexer_2_out;
  wire [31:0] bit_extender_2_out, bit_extender_9_out, multiplexer_3_out, negator_1_out;

  Multiplexer #(.width(3)) multiplexer_1 (
    .in0(Instruction[2:0]), .in1(Instruction[10:8]), .out(RdMux), .sel(Instruction[13]));
  assign bit_extender_1_out = {{5{1'b0}}, Instruction[8:6]};  // Bit_Extender bit_extender_1
  and and_1 (and_1_out, ~Instruction[13], ~Instruction[12], ~Instruction[11]);  // AND_Gate
  and and_2 (and_2_out, ~Instruction[13], ~Instruction[12], Instruction[11]);  // AND_Gate
  or or_1 (UseImm5, and_1_out, and_2_out, and_3_out);
  and and_3 (and_3_out, ~Instruction[13], Instruction[12], ~Instruction[11]);  // AND_Gate
  and and_4 (and_4_out, ~Instruction[13], Instruction[12], Instruction[11], ~Instruction[10], ~Instruction[9]);  // AND_Gate
  and and_5 (and_5_out, ~Instruction[13], Instruction[12], Instruction[11], ~Instruction[10], Instruction[9]);  // AND_Gate
  and and_6 (and_6_out, ~Instruction[13], Instruction[12], Instruction[11], Instruction[10], ~Instruction[9]);  // AND_Gate
  and and_7 (and_7_out, ~Instruction[13], Instruction[12], Instruction[11], Instruction[10], Instruction[9]);  // AND_Gate
  and and_8 (IsMOV, Instruction[13], ~Instruction[12], ~Instruction[11]);  // AND_Gate
  and and_9 (and_9_out, Instruction[13], ~Instruction[12], Instruction[11]);  // AND_Gate
  and and_10 (and_10_out, Instruction[13], Instruction[12], ~Instruction[11]);  // AND_Gate
  and and_11 (and_11_out, Instruction[13], Instruction[12], Instruction[11]);
  or or_2 (UseRm, and_4_out, and_5_out);
  nor nor_1 (UseRn, IsMOV, and_9_out, and_10_out, and_11_out);
  or or_3 (Rdn, and_10_out, and_11_out);
  Multiplexer #(.enable("true"), .width(8)) multiplexer_2 (
    .in0(Instruction[7:0]), .in1(bit_extender_1_out), .out(multiplexer_2_out), .sel(UseRn), .en(UseImm32));
  assign bit_extender_2_out = {{24{1'b0}}, multiplexer_2_out};  // Bit_Extender bit_extender_2
  Priority_Encoder #(.select(4)) priority_encoder_1 (
    .in0(and_1_out), .in1(and_2_out), .in2(and_3_out), .in3(and_4_out), .in4(and_5_out), .in5(and_6_out),
    .in6(and_7_out), .in7(IsMOV), .in8(and_9_out), .in9(and_10_out), .in10(and_11_out),
    .out(priority_encoder_1_out));  // open: in11, in12, in13, in14, in15, gs, en_out, en_in
  nor nor_2 (UseImm32, UseRm, UseImm5);
  or or_4 (Carry_t, and_5_out, and_7_out, and_11_out);
  Negator #(.width(32)) negator_1 (.in(bit_extender_2_out), .out(negator_1_out));
  Multiplexer #(.width(32)) multiplexer_3 (
    .in0(bit_extender_2_out), .in1(negator_1_out), .out(multiplexer_3_out), .sel(IsMOV));
  nor nor_3 (FlagsMask[0], IsMOV, UseImm5);
  not not_1 (FlagsMask[1], IsMOV);
  Multiplexer #(.width(3)) multiplexer_4 (.in0(Instruction[5:3]), .in1(RdMux), .out(multiplexer_4_out), .sel(Rdn));
  Multiplexer #(.select(4), .width(4)) multiplexer_5 (
    .in0(4'b0010), .in1(4'b0011), .in2(4'b0100), .in3(4'b0101), .in4(4'b0110), .in5(4'b0101), .in6(4'b0110),
    .in7(4'b1001), .in8(4'b1010), .in9(4'b0101), .in10(4'b0110), .out(multiplexer_5_out),
    .sel(priority_encoder_1_out));  // open: in11, in12, in13, in14, in15
  assign bit_extender_3_out = {{2{UseRm}}, UseRm};  // Bit_Extender bit_extender_3
  or or_5 (or_5_out, UseRn, Rdn);
  assign bit_extender_4_out = {{4{UseImm5}}, UseImm5};  // Bit_Extender bit_extender_4
  assign bit_extender_5_out = {{3{Enable}}, Enable};  // Bit_Extender bit_extender_5
  assign Flags_Update_Mask = bit_extender_5_out & {2'b11, FlagsMask};  // AND_Gate and_12, 4 bits wide
  and and_13 (Carry, Enable, Carry_t);
  and and_14 (Imm32_Enable, Enable, UseImm32);
  assign bit_extender_6_out = {{2{Enable}}, Enable};  // Bit_Extender bit_extender_6
  assign bit_extender_7_out = {{2{or_5_out}}, or_5_out};  // Bit_Extender bit_extender_7
  assign and_15_out = bit_extender_7_out & multiplexer_4_out;  // AND_Gate and_15, 3 bits wide
  assign bit_extender_8_out = {{2{Enable}}, Enable};  // Bit_Extender bit_extender_8
  assign Rd = bit_extender_8_out & RdMux;  // AND_Gate and_16, 3 bits wide
  assign and_17_out = bit_extender_4_out & Instruction[10:6];  // AND_Gate and_17, 5 bits wide
  assign bit_extender_9_out = {{31{Enable}}, Enable};  // Bit_Extender bit_extender_9
  assign Imm32 = bit_extender_9_out & multiplexer_3_out;  // AND_Gate and_18, 32 bits wide
  assign ALU_Opcode = multiplexer_5_out & bit_extender_10_out;  // AND_Gate and_19, 4 bits wide
  assign bit_extender_10_out = {{3{Enable}}, Enable};  // Bit_Extender bit_extender_10
  assign bit_extender_11_out = {{2{Enable}}, Enable};  // Bit_Extender bit_extender_11
  assign Rn = bit_extender_11_out & and_15_out;  // AND_Gate and_20, 3 bits wide
  assign bit_extender_12_out = {{4{Enable}}, Enable};  // Bit_Extender bit_extender_12
  assign Rm = bit_extender_6_out & bit_extender_3_out & Instruction[8:6];  // AND_Gate and_21, 3 bits wide
  assign Imm5 = bit_extender_12_out & and_17_out;  // AND_Gate and_22, 5 bits wide

  // Other names for the same wires on the sheet: Imm5_t[4:0] = Instruction[10:6]; b13 = Instruction[13]

  // Notes on the sheet:
  //   Note: ALU uses Rn register for shifts. Use Rn instead of Rm for shifts (immediate) here too
  //   Note 3: Imm32_Enable forces the use of the immediate for Rm register
  //   Note 2: MOV uses RSB ALU opcode with Imm8 reversed so that it is copied to output register
  //   Pull output low on Enable = 0
  //   Enable carry for SUB since it is reversed in ALU
  //   ALU will use Imm32 instead of Rm
  //   only ADD and SUB use Rm
endmodule
